# Fritzing sketch e1_twitter (saved by Fritzing 0.9.2b)
breadboards: 1

parts:
  Part1 = Arduino Yun
  R2 = Resistor [tolerance=±5% resistance=10k package=THT]  # not connected
  S2 = Square Pushbutton

nets:
  N1: Part1.5V, S2.leg1
  N2: Part1.D2, S2.leg0
