# Fritzing sketch e2_temperature_twitter (saved by Fritzing 0.9.2b)
breadboards: 1

parts:
  Part1 = Arduino Yun
  R2 = Resistor [tolerance=±5% resistance=10k package=THT]  # not connected
  S2 = Square Pushbutton
  LED1 = Adafruit_FLORA_RGB_Smart_Pixel

nets:
  N1: Part1.5V, S2.leg1, LED1.connector1
  N2: Part1.D9_PWM, LED1.connector2
  N3: Part1.D2, S2.leg0
  N4: Part1.GND, LED1.connector3
