# Fritzing sketch e3_clothesline_test (saved by Fritzing 0.9.2b)
breadboards: 1

parts:
  Part1 = Arduino Yun
  J3 = Basic Servo
  R2 = Resistor [tolerance=±5% resistance=10k package=THT]  # not connected
  S2 = Square Pushbutton

nets:
  5V: Part1.5V, J3.vcc, S2.leg1
  N1: Part1.D2, S2.leg0
  N2: Part1.D3_PWM, J3.pulse
  GND: Part1.GND, J3.gnd

notes:
  mirco servo
  pull in clothesline
