# Fritzing sketch e3_fan_test (saved by Fritzing 0.9.2b)
breadboards: 1

parts:
  Part1 = Arduino Yun
  R2 = Resistor [tolerance=±5% resistance=10k package=THT]  # not connected
  S2 = Square Pushbutton
  M2 = DC Motor
  Q4 = NPN-Transistor [package="TO92 [THT]"]
  R3 = Resistor [tolerance=±5% resistance=1k package="2512 [SMD]"]

nets:
  N1: Part1.5V, S2.leg1, M2.pin_2
  N2: Part1.D2, S2.leg0
  N3: Part1.D6_PWM, R3.Pin_0
  N4: Part1.GND, Q4.E
  N5: M2.pin_1, Q4.C
  N6: Q4.B, R3.Pin_1

notes:
  DC motor
  turn on fan
