# Fritzing sketch e3_fullhouse_home_Yun (saved by Fritzing 0.9.2b)
breadboards: 7

parts:
  L1 = Solenoid
  M1 = DC Motor
  J2 = Basic Servo
  U2 = TMP36 [package=to-92]
  R3 = Resistor [tolerance=±5% resistance=150k package="2512 [SMD]"]
  Part2 = Arduino Yun
  Q4 = Basic FET N-Channel [package="TO220 [THT]"]
  R4 = Resistor [tolerance=±5% resistance=150k package="2512 [SMD]"]
  L2 = Solenoid
  Q5 = Basic FET N-Channel [package="TO220 [THT]"]
  J5 = MicroServo
  Q6 = Basic FET N-Channel [package="TO220 [THT]"]
  R5 = Resistor [tolerance=±5% resistance=150k package="2512 [SMD]"]

nets:
  N1: L1.pin1, Q4.drain
  VCC: L1.pin2, M1.pin_2, J2.vcc, U2.VCC, Part2.5V, L2.pin2, J5.vcc
  N2: M1.pin_1, Q6.drain
  GND: J2.gnd, U2.GND, R3.Pin_0, Part2.GND, Q4.source, R4.Pin_0, Q5.source, J5.gnd, Q6.source, R5.Pin_0
  N3: J2.pulse, Part2.D3_PWM
  N4: U2.VOUT, Part2.A0
  N5: R3.Pin_1, Part2.D10_PWM/SS, Q4.gate
  N6: Part2.D9_PWM, R4.Pin_1, Q5.gate
  N7: Part2.D4, J5.pulse
  N8: Part2.D6_PWM, Q6.gate, R5.Pin_1
  N9: L2.pin1, Q5.drain

notes:
  solenoid
  water plant
  solenoid
  vent room
  DC motor
  turn on fan
  Servo
  Down shades
  Continuous servo
  pull in clothesline
  temperature sensor

custom parts:
  MicroServo: A generic servo.
