# Fritzing sketch e3_roofvent_test (saved by Fritzing 0.9.2b)
breadboards: 1

parts:
  Part2 = Arduino Yun
  R5 = Resistor [tolerance=±5% resistance=150k package="2512 [SMD]"]
  R6 = Resistor [tolerance=±5% resistance=10k package=THT]  # not connected
  S3 = Square Pushbutton
  L3 = Solenoid
  Q6 = Basic FET N-Channel [package="TO220 [THT]"]

nets:
  N1: Part2.5V, S3.leg1, L3.pin2
  N2: Part2.D9_PWM, R5.Pin_1, Q6.gate
  N3: Part2.D2, S3.leg0
  N4: Part2.GND, R5.Pin_0, Q6.source
  N5: L3.pin1, Q6.drain
