# Fritzing sketch e3_watering_test (saved by Fritzing 0.9.2b)
breadboards: 1

parts:
  R2 = Resistor [tolerance=±5% resistance=10k package=THT]  # not connected
  S2 = Square Pushbutton
  Q4 = NPN-Transistor [package="TO92 [THT]"]
  R3 = Resistor [tolerance=±5% resistance=1k package="2512 [SMD]"]
  Part1 = Arduino Yun
  L3 = Solenoid

nets:
  N1: S2.leg0, Part1.D2
  N2: S2.leg1, Part1.5V, L3.pin2
  N3: Q4.E, Part1.GND
  N4: Q4.B, R3.Pin_1
  N5: Q4.C, L3.pin1
  N6: R3.Pin_0, Part1.D10_PWM/SS

notes:
  solenoid
  vent room
