# Fritzing sketch e3_windowshade_test (saved by Fritzing 0.9.2b)
breadboards: 1

parts:
  Part1 = Arduino Yun
  R2 = Resistor [tolerance=±5% resistance=10k package=THT]  # not connected
  S2 = Square Pushbutton
  J4 = MicroServo

nets:
  5V: Part1.5V, S2.leg1, J4.vcc
  N1: Part1.D2, S2.leg0
  N2: Part1.D4, J4.pulse
  GND: Part1.GND, J4.gnd

custom parts:
  MicroServo: A generic servo.
