# Fritzing sketch e4_exercise_sensor (saved by Fritzing 0.9.2b)
breadboards: 1

parts:
  R4 = Resistor [tolerance=±5% resistance=10k package="2512 [SMD]"]
  R5 = Basic Flex Resistor
  Part2 = Genuino Uno (Rev3)
  BLUEFRUIT3 = Adafruit Bluefruit EZ-LINK v1.0

nets:
  N1: R4.Pin_0, R5.pin_1, Part2.A0
  GND: R4.Pin_1, Part2.GND, BLUEFRUIT3.GND
  5V: R5.Pin_2, Part2.5V, BLUEFRUIT3.Vin
  N2: Part2.D10_PWM/SS, BLUEFRUIT3.TX
  N3: Part2.D11_PWM/MOSI, BLUEFRUIT3.RX

custom parts:
  Genuino Uno (Rev3): The Arduino Uno is a microcontroller board based on the ATmega328 (datasheet). It has 14 digital input/output pins (of which 6 can be used as PWM outputs), 6 analog inputs, a 16 MHz ceramic resonator, a USB connection, a power jack, an ICSP header, and a reset button. It contains everything needed to support the microcontroller; simply connect it to a computer with a USB cable or power it with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
  Adafruit Bluefruit EZ-LINK v1.0: Bluefruit EZ-LINK, Bluetooth Serial Link & Arduino Programmer
