# Fritzing sketch e5_carcounter (saved by Fritzing 0.9.2b)
breadboards: 1

parts:
  Part1 = Arduino Yun
  LED1 = Adafruit_FLORA_RGB_Smart_Pixel
  J1 = Basic Force Sensing Resistor (FSR) [package=THT]
  R4 = Resistor [tolerance=±5% resistance=10k package="2512 [SMD]"]

nets:
  N1: Part1.A0, J1.pin_0, R4.Pin_0
  N2: Part1.D6_PWM, LED1.connector2
  N3: Part1.5V, LED1.connector1, J1.pin_1
  N4: Part1.GND, LED1.connector3, R4.Pin_1
