# Fritzing sketch e5_carparkchecker (saved by Fritzing 0.9.2b)
breadboards: 1

parts:
  Part1 = Arduino Yun
  LED1 = Adafruit_FLORA_RGB_Smart_Pixel
  R4 = Resistor [tolerance=±5% resistance=10k package="2512 [SMD]"]
  R5 = Photocell (LDR) [package=THT]

nets:
  N1: Part1.A0, R4.Pin_0, R5.pin_0
  N2: Part1.D6_PWM, LED1.connector2
  N3: Part1.5V, LED1.connector1, R5.pin_1
  N4: Part1.GND, LED1.connector3, R4.Pin_1
