# Fritzing sketch e5_coupon_dispenser (saved by Fritzing 0.9.2b)
breadboards: 1

parts:
  Part1 = Arduino Yun
  LED1 = Adafruit_FLORA_RGB_Smart_Pixel
  R1 = Resistor [tolerance=±5% resistance=10k package="0402 [SMD]"]

nets:
  N1: Part1.D2, R1.Pin_1
  N2: Part1.D4, R1.Pin_0
  N3: Part1.D6_PWM, LED1.connector2
  N4: Part1.5V, LED1.connector1
  N5: Part1.GND, LED1.connector3
