# Fritzing sketch e5_seatchecker (saved by Fritzing 0.9.2b)
breadboards: 1

parts:
  Part1 = Arduino Yun
  LED1 = Adafruit_FLORA_RGB_Smart_Pixel
  U1 = TMP36 [package=to-92]

nets:
  N1: Part1.A0, U1.VOUT
  N2: Part1.D6_PWM, LED1.connector2
  5V: Part1.5V, LED1.connector1, U1.VCC
  GND: Part1.GND, LED1.connector3, U1.GND
