# Fritzing sketch ex_oil_probe (saved by Fritzing 0.9.2b)
breadboards: 1

parts:
  Part1 = Arduino Yun
  R4 = Resistor [tolerance=±5% resistance=10k package="2512 [SMD]"]
  R5 = Resistor [tolerance=±5% resistance=10k package="2512 [SMD]"]
  R6 = Resistor [tolerance=±5% resistance=10k package="2512 [SMD]"]
  R7 = Resistor [tolerance=±5% resistance=10k package="2512 [SMD]"]

nets:
  N1: Part1.A0, R7.Pin_0
  N2: Part1.A1, R6.Pin_0
  N3: Part1.A2, R5.Pin_0
  N4: Part1.A3, R4.Pin_0
  N5: Part1.GND, R4.Pin_1, R5.Pin_1, R6.Pin_1, R7.Pin_1
